# Fritzing sketch Arduino na protoboard (saved by Fritzing 0.9.4)
breadboards: 1

parts:
  U1 = atmega328 [package=dip]
  C1 = Ceramic Capacitor [capacitance="100 nF" package="1206 [SMD, multilayer]"]
  S1 = Pushbutton [package="[SMD]"]
  R1 = Resistor [tolerance=±5% resistance=10k package=THT]
  Y1 = CRYSTAL [package=hc49u-v]
  C2 = Capacitor [package=cap-pth-small2]
  C3 = Capacitor [package=cap-pth-small2]
  R2 = Resistor [tolerance=±5% resistance=220 package=THT]
  LED1 = LED - 5mm [color="Red (633nm)" package="5 mm [THT]"]
  J2 = female pin header, 4 pins [form="♀ (female)"]
  J1 = female pin header, 6 pins [form="♀ (female)"]
  J4 = female pin header, 5 pins [form="♀ (female)"]
  J3 = female pin header, 5 pins [form="♀ (female)"]

nets:
  N1: U1.RESET, S1.Pin_1, S1.Pin_2, R1.Pin_0
  N2: U1.D0_(RX), J3.pin1
  N3: U1.D1_(TX), J3.pin2
  N4: U1.D2, J3.pin3
  N5: U1.D3_(PWM), J3.pin4
  N6: U1.D4, J3.pin5
  N7: U1.VCC, U1.AVCC, U1.AREF, C1.0, R1.Pin_1
  N8: U1.GND, C1.1, S1.Pin_3, S1.Pin_4, C2.2, C3.1, R2.Pin_0
  N9: U1.XLAT1, Y1.1, C3.2
  N10: U1.XLAT2, Y1.2, C2.1
  N11: U1.D5_(PWM), J2.pin1
  N12: U1.D6_(PWM), J2.pin2
  N13: U1.D7, J2.pin3
  N14: U1.D8, J2.pin4
  N15: U1.D9_(PWM), J4.pin5
  N16: U1.D10_(PWM), J4.pin4
  N17: U1.D11_(PWM), J4.pin3
  N18: U1.D12, J4.pin2
  N19: U1.D13, LED1.anode, J4.pin1
  N20: U1.A0, J1.pin6
  N21: U1.A1, J1.pin5
  N22: U1.A2, J1.pin4
  N23: U1.A3, J1.pin3
  N24: U1.A4, J1.pin2
  N25: U1.A5, J1.pin1
  N26: R2.Pin_1, LED1.cathode
